# Fritzing sketch smart_bottle (saved by Fritzing 0.9.3b)
breadboards: 1

parts:
  U1 = NodeMCU V1.0
  R1 = Resistor [tolerance=±5% resistance=10k package=THT]
  R2 = Photocell (LDR) [package=THT]
  DS1 = DS18B20 1-Wire Temperature Sensor [part_number=DS18B20]
  R3 = Resistor [tolerance=±5% resistance=220 package=THT]
  R4 = Resistor [tolerance=±5% resistance=220 package=THT]
  R5 = Resistor [tolerance=±5% resistance=220 package=THT]
  LED1 = RGB LED (com. anode, rbg) [package="5 mm [THT]"]

nets:
  N1: U1.D0, R5.Pin_1
  N2: U1.D4, R4.Pin_1
  3V3: U1.3V3, R2.pin_1, DS1.VDD, LED1.common_anode
  N3: U1.GND, R1.Pin_1, DS1.DQ
  N4: U1.D6, DS1.GND
  N5: U1.D7, R3.Pin_1
  N6: U1.A0, R1.Pin_0, R2.pin_0
  N7: R3.Pin_0, LED1.green_cathode
  N8: R4.Pin_0, LED1.blue_cathode
  N9: R5.Pin_0, LED1.red_cathode

custom parts:
  NodeMCU V1.0: ESP8266 based NodeMCU
